# Fritzing sketch pump-relay (saved by Fritzing 0.9.3b)
breadboards: 1

parts:
  Onderdeel2 = Adafruit Latching Mini Relay FeatherWing [part_number="Adafruit #2923"]
  J1 = Power Jack [package=power_jack_smd]
  M1 = DC Motor
  Onderdeel3 = Adafruit Feather HUZZAH ESP8266 [part_number="Adafruit #2821"]
  S1 = SWITCH-MOMENTARY-2 [package=tactile-pth-12mm]
  Grove1 = Grove Temperature Sensor
  R1 = Resistor [tolerance=±5% resistance=10k package="2512 [SMD]"]
  R2 = Resistor [tolerance=±5% resistance=470 package="2512 [SMD]"]

nets:
  N1: Onderdeel2.E, Onderdeel2.UNSET, Onderdeel3.GPIO13/MOSI
  N2: Onderdeel2.C, Onderdeel2.SET, Onderdeel3.GPIO12/MISO
  N3: Onderdeel2.3.3V, Onderdeel2.COM, J1.PWR
  GND: Onderdeel2.GND, J1.GND, M1.pin_2
  N4: Onderdeel2.NO, M1.pin_1
  N5: Onderdeel3.ADC, R1.Pin_0, R2.Pin_1
  GND_2: Onderdeel3.GND, S1.1, Grove1.GND, R2.Pin_0
  3.3V: Onderdeel3.3.3V, Grove1.VCC
  N6: Onderdeel3.GPIO2, S1.2
  N7: Grove1.SIG, R1.Pin_1

notes:
  Grovehumidity sensor not in palette. Showing temperature sensor instead.
  Wiring button GND to feather directly and not the power rail improved sensor value reading when pressing button

custom parts:
  Adafruit Latching Mini Relay FeatherWing: A Feather board without ambition is a Feather board without FeatherWings! This is the Latching Mini Relay FeatherWing. It gives you power to control, and control over power. Put simply, you can now turn on and off lamps, fans, solenoids, and other small appliances that run on up to 250VAC or DC power using any Feather board. The are two 'flavors' of these FeatherWings, this is the Latching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
  Adafruit Feather HUZZAH ESP8266: his is the Adafruit Feather HUZZAH ESP8266 - our take on an 'all-in-one' ESP8266 WiFi development board with built in USB and battery charging. Its an ESP8266 WiFi module with all the extras you need, ready to rock! We have other boards in the Feather family, check'em out here. At the Feather HUZZAH's heart is an ESP8266 WiFi microcontroller clocked at 80 MHz and at 3.3V logic. This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
